// Logisim project Pierce_Clayton.circ as structural Verilog: 16 circuits, main circuit main
module main (
);

  wire CLK, CNT_2_ld, CNT_2_str, CNT_mux, comparator_1_eq, FLUSH, or_1_out, Stall1, Stall2, wbcontrol_1_mux,
       wbcontrol_1_wren;
  wire [1:0] CNT_func, PCMO, PCMux;
  wire [3:0] ex_mem_buffer_1_rxout, ExeOP, ExeRX, IDOP, IDRX, IDRY, IDRZ, mem_wb_buffer_1_opout,
       mem_wb_buffer_1_rxout, MEMOP, multiplexer_3_out_3, multiplexer_3_out_4, R2;
  wire [7:0] multiplexer_3_out;
  wire [15:0] multiplexer_3_out_2;
  wire [19:4] if_idrr_buffer_1_imout;
  wire [23:0] adder_1_out, adder_2_out, ex_mem_buffer_1_addout, idrr_ex_buffer_1_pc_1out,
       if_idrr_buffer_1_pc_1out, multiplexer_1_out, PC_q, SRED_2_dout, SRED_dout;
  wire [31:0] alu_1_out, dual_ported_register_file_1_out1, dual_ported_register_file_1_out2,
       ex_mem_buffer_1_aluout, ex_mem_buffer_1_datain_2, idrr_ex_buffer_1_aout, idrr_ex_buffer_1_bout,
       idrr_ex_buffer_1_sexout, mem_wb_buffer_1_addrout, mem_wb_buffer_1_datain_2, multiplexer_2_out,
       ram_1_data, ram_2_data, SEXT_dout;

  Register #(.width(24)) PC (.D(multiplexer_1_out), .Q(PC_q), .clk(CLK));  // open: en, clr
  Adder #(.width(24)) adder_1 (.a(PC_q), .b(24'h1), .out(adder_1_out));  // open: cin, cout
  Clock clock_1 (.out(CLK));
  RAM #(.addrWidth(24), .dataWidth(32)) ram_1 (.addr(PC_q), .data(ram_1_data), .clk(CLK));  // open: sel, ld, clr
  IDRRControl idrrcontrol_1 (.RX(IDRX), .RZ(IDRZ), .OPCode(IDOP), .RX_RZ(R2));
  Multiplexer #(.select(2), .width(24), .enable("false")) multiplexer_1 (
    .in0(adder_1_out), .in1(ex_mem_buffer_1_addout), .in2(SRED_2_dout), .in3(PC_q), .out(multiplexer_1_out),
    .sel(PCMO));
  IF_IDRR_Buffer if_idrr_buffer_1 (
    .PC_1in(adder_1_out), .IMin(ram_1_data), .CLK(CLK), .CLR(FLUSH), .Stall(Stall1),
    .PC_1out(if_idrr_buffer_1_pc_1out), .IMout({IDOP, IDRX, IDRY, if_idrr_buffer_1_imout, IDRZ}));
  Hex_Digit_Display hex_digit_display_1 (.value(R2));  // open: dp
  StallCheck stallcheck_1 (
    .PCMuxout(PCMO), .Stall1(Stall1), .Stall2(Stall2), .OPCode(ExeOP), .RX(ExeRX), .RY(IDRY), .RZ(IDRZ),
    .ID_RROP(IDOP), .PCMux(PCMux));
  SEXT SEXT (.Din({IDOP, IDRX, IDRY, if_idrr_buffer_1_imout, IDRZ}), .Dout(SEXT_dout));
  Dual_Ported_Register_File dual_ported_register_file_1 (
    .CLK(CLK), .WrEN(wbcontrol_1_wren), .OUT1(dual_ported_register_file_1_out1),
    .WrREGNO(mem_wb_buffer_1_rxout), .RdREGNO1(IDRY), .RdREGNO2(R2), .OUT2(dual_ported_register_file_1_out2),
    .INPUT({multiplexer_3_out_4, multiplexer_3_out_3, multiplexer_3_out, multiplexer_3_out_2}));
  or or_1 (or_1_out, 1'b0, Stall2);
  MUXBox muxbox_1 (.Sel(PCMux), .FLUSH(FLUSH), .EQ(comparator_1_eq), .OPCode(MEMOP));
  Adder #(.width(24)) adder_2 (.a(idrr_ex_buffer_1_pc_1out), .b(SRED_dout), .out(adder_2_out));  // open: cin, cout
  SRED SRED (.Din(idrr_ex_buffer_1_sexout), .Dout(SRED_dout));
  IDRR_EX_Buffer idrr_ex_buffer_1 (
    .PC_1(if_idrr_buffer_1_pc_1out), .Ain(dual_ported_register_file_1_out1),
    .Bin(dual_ported_register_file_1_out2), .SEXin(SEXT_dout), .OPin(IDOP), .RXin(IDRX), .CLK(CLK),
    .CLR(FLUSH), .in_7(or_1_out), .PC_1out(idrr_ex_buffer_1_pc_1out), .Aout(idrr_ex_buffer_1_aout),
    .Bout(idrr_ex_buffer_1_bout), .SEXout(idrr_ex_buffer_1_sexout), .OPout(ExeOP), .RXout(ExeRX));
  EXControl CNT (.OPCode(ExeOP), .MUX(CNT_mux), .func(CNT_func));
  Multiplexer #(.width(32), .enable("false")) multiplexer_2 (
    .in0(idrr_ex_buffer_1_bout), .in1(idrr_ex_buffer_1_sexout), .out(multiplexer_2_out), .sel(CNT_mux));
  Hex_Digit_Display hex_digit_display_2 (.value(mem_wb_buffer_1_rxout));  // open: dp
  ALU alu_1 (.FUNC(CNT_func), .A(idrr_ex_buffer_1_aout), .B(multiplexer_2_out), .OUT(alu_1_out));
  Comparator #(.width(32)) comparator_1 (
    .a({32{1'b0}}), .b(ex_mem_buffer_1_aluout), .eq(comparator_1_eq));  // open: gt, lt
  EX_MEM_Buffer ex_mem_buffer_1 (
    .ADDin(adder_2_out), .ALUin(alu_1_out), .DATAin(idrr_ex_buffer_1_bout), .OPin(ExeOP), .RXin(ExeRX),
    .CLK(CLK), .ADDout(ex_mem_buffer_1_addout), .ALUout(ex_mem_buffer_1_aluout),
    .DATAin_2(ex_mem_buffer_1_datain_2), .OPout(MEMOP), .RXout(ex_mem_buffer_1_rxout));
  Hex_Digit_Display hex_digit_display_3 (.value(multiplexer_3_out_4));  // open: dp
  SRED SRED_2 (.Din(ex_mem_buffer_1_aluout), .Dout(SRED_2_dout));
  MEMControl CNT_2 (.OPCode(MEMOP), .STR(CNT_2_str), .LD(CNT_2_ld));
  Hex_Digit_Display hex_digit_display_4 (.value(multiplexer_3_out[7:4]));  // open: dp
  Hex_Digit_Display hex_digit_display_5 (.value(multiplexer_3_out_3));  // open: dp
  Hex_Digit_Display hex_digit_display_6 (.value(multiplexer_3_out[3:0]));  // open: dp
  RAM #(.addrWidth(24), .dataWidth(32), .bus("separate")) ram_2 (
    .addr(SRED_2_dout), .din(ex_mem_buffer_1_datain_2), .data(ram_2_data), .str(CNT_2_str), .clk(CLK),
    .ld(CNT_2_ld));  // open: sel, clr
  Hex_Digit_Display hex_digit_display_7 (.value(multiplexer_3_out_2[15:12]));  // open: dp
  MEM_WB_Buffer mem_wb_buffer_1 (
    .DATAin(ram_2_data), .ADDRin(ex_mem_buffer_1_aluout), .OPin(MEMOP), .RXin(ex_mem_buffer_1_rxout),
    .CLK(CLK), .DATAin_2(mem_wb_buffer_1_datain_2), .ADDRout(mem_wb_buffer_1_addrout),
    .OPout(mem_wb_buffer_1_opout), .RXout(mem_wb_buffer_1_rxout));
  WBControl wbcontrol_1 (.OPCode(mem_wb_buffer_1_opout), .WrEN(wbcontrol_1_wren), .MUX(wbcontrol_1_mux));
  Hex_Digit_Display hex_digit_display_8 (.value(multiplexer_3_out_2[11:8]));  // open: dp
  Multiplexer #(.width(32), .enable("false")) multiplexer_3 (
    .in0(mem_wb_buffer_1_datain_2), .in1(mem_wb_buffer_1_addrout),
    .out({multiplexer_3_out_4, multiplexer_3_out_3, multiplexer_3_out, multiplexer_3_out_2}),
    .sel(wbcontrol_1_mux));
  Hex_Digit_Display hex_digit_display_9 (.value(multiplexer_3_out_2[7:4]));  // open: dp
  Hex_Digit_Display hex_digit_display_10 (.value(multiplexer_3_out_2[3:0]));  // open: dp

  // Notes on the sheet:
  //   RX
  //   RX
  //   RX
  //   Should the soln go after the EX/MEM Buff or before?
endmodule

module Dual_Ported_Register_File (
  input  CLK,
  input  WrEN,
  input  [3:0] WrREGNO,
  input  [3:0] RdREGNO1,
  input  [3:0] RdREGNO2,
  input  [31:0] INPUT,
  output [31:0] OUT1,
  output [31:0] OUT2
);

  wire En_a0, En_a1, En_a2, En_a3, En_a4, En_at, En_fp, En_k0, En_ra, En_s0, En_s1, En_s2, En_s3, En_sp,
       En_v0;
  wire [31:0] a0, a1, a2, a3, a4, at, fp, k0, ra, s0, s1, s2, s3, sp, v0, zero;

  Decoder #(.select(4), .disabled(0)) decoder_1 (
    .out1(En_at), .out2(En_v0), .out3(En_a0), .out4(En_a1), .out5(En_a2), .out6(En_a3), .out7(En_a4),
    .out8(En_s0), .out9(En_s1), .out10(En_s2), .out11(En_s3), .out12(En_k0), .out13(En_sp), .out14(En_fp),
    .out15(En_ra), .sel(WrREGNO), .en(WrEN));  // open: out0
  Register #(.width(32)) u_zero (.D(INPUT), .en(1'b0), .Q(zero), .clk(CLK));  // open: clr
  Register #(.width(32)) u_at (.D(INPUT), .en(En_at), .Q(at), .clk(CLK));  // open: clr
  Register #(.width(32)) u_v0 (.D(INPUT), .en(En_v0), .Q(v0), .clk(CLK));  // open: clr
  Register #(.width(32)) u_a0 (.D(INPUT), .en(En_a0), .Q(a0), .clk(CLK));  // open: clr
  Register #(.width(32)) u_a1 (.D(INPUT), .en(En_a1), .Q(a1), .clk(CLK));  // open: clr
  Register #(.width(32)) u_a2 (.D(INPUT), .en(En_a2), .Q(a2), .clk(CLK));  // open: clr
  Register #(.width(32)) u_a3 (.D(INPUT), .en(En_a3), .Q(a3), .clk(CLK));  // open: clr
  Register #(.width(32)) u_a4 (.D(INPUT), .en(En_a4), .Q(a4), .clk(CLK));  // open: clr
  Multiplexer #(.select(4), .width(32), .disabled(0), .enable("false")) multiplexer_1 (
    .in0(zero), .in1(at), .in2(v0), .in3(a0), .in4(a1), .in5(a2), .in6(a3), .in7(a4), .in8(s0), .in9(s1),
    .in10(s2), .in11(s3), .in12(k0), .in13(sp), .in14(fp), .in15(ra), .out(OUT2), .sel(RdREGNO2));
  Register #(.width(32)) u_s0 (.D(INPUT), .en(En_s0), .Q(s0), .clk(CLK));  // open: clr
  Register #(.width(32)) u_s1 (.D(INPUT), .en(En_s1), .Q(s1), .clk(CLK));  // open: clr
  Register #(.width(32)) u_s2 (.D(INPUT), .en(En_s2), .Q(s2), .clk(CLK));  // open: clr
  Register #(.width(32)) u_s3 (.D(INPUT), .en(En_s3), .Q(s3), .clk(CLK));  // open: clr
  Register #(.width(32)) u_k0 (.D(INPUT), .en(En_k0), .Q(k0), .clk(CLK));  // open: clr
  Register #(.width(32)) u_sp (.D(INPUT), .en(En_sp), .Q(sp), .clk(CLK));  // open: clr
  Register #(.width(32)) u_fp (.D(INPUT), .en(En_fp), .Q(fp), .clk(CLK));  // open: clr
  Register #(.width(32)) u_ra (.D(INPUT), .en(En_ra), .Q(ra), .clk(CLK));  // open: clr
  Multiplexer #(.select(4), .width(32), .disabled(0), .enable("false")) multiplexer_2 (
    .in0(zero), .in1(at), .in2(v0), .in3(a0), .in4(a1), .in5(a2), .in6(a3), .in7(a4), .in8(s0), .in9(s1),
    .in10(s2), .in11(s3), .in12(k0), .in13(sp), .in14(fp), .in15(ra), .out(OUT1), .sel(RdREGNO1));

  // Notes on the sheet:
  //   DO NOT MODIFY THIS FILE
endmodule

module IF_IDRR_Buffer (
  input  [23:0] PC_1in,
  input  [31:0] IMin,
  input  CLK,
  input  CLR,
  input  Stall,
  output [23:0] PC_1out,
  output [31:0] IMout
);

  wire not_1_out;

  Register #(.width(24)) register_1 (.D(PC_1in), .en(not_1_out), .Q(PC_1out), .clk(CLK), .clr(CLR));
  Register #(.width(32)) register_2 (.D(IMin), .en(not_1_out), .Q(IMout), .clk(CLK), .clr(CLR));
  not not_1 (not_1_out, Stall);
endmodule

module IDRR_EX_Buffer (
  input  [23:0] PC_1,
  input  [31:0] Ain,
  input  [31:0] Bin,
  input  [31:0] SEXin,
  input  [3:0] OPin,
  input  [3:0] RXin,
  input  in_7,
  input  CLK,
  input  CLR,
  output [23:0] PC_1out,
  output [31:0] Aout,
  output [31:0] Bout,
  output [31:0] SEXout,
  output [3:0] OPout,
  output [3:0] RXout
);

  wire not_1_out;
  wire [3:0] register_5_q, register_6_q;
  wire [23:0] register_1_q;
  wire [31:0] register_2_q, register_3_q, register_4_q;

  Register #(.width(24)) register_1 (.D(PC_1), .en(not_1_out), .Q(register_1_q), .clk(CLK), .clr(CLR));
  Register #(.width(32)) register_2 (.D(Ain), .en(not_1_out), .Q(register_2_q), .clk(CLK), .clr(CLR));
  Register #(.width(32)) register_3 (.D(Bin), .en(not_1_out), .Q(register_3_q), .clk(CLK), .clr(CLR));
  Register #(.width(32)) register_4 (.D(SEXin), .en(not_1_out), .Q(register_4_q), .clk(CLK), .clr(CLR));
  Register #(.width(4)) register_5 (.D(OPin), .Q(register_5_q), .clk(CLK), .clr(CLR));  // open: en
  Register #(.width(4)) register_6 (.D(RXin), .en(not_1_out), .Q(register_6_q), .clk(CLK), .clr(CLR));
  not not_1 (not_1_out, in_7);
  Multiplexer #(.width(24), .enable("false")) multiplexer_1 (
    .in0({24{1'b0}}), .in1(register_1_q), .out(PC_1out), .sel(not_1_out));
  Multiplexer #(.width(32), .enable("false")) multiplexer_2 (
    .in0({32{1'b0}}), .in1(register_2_q), .out(Aout), .sel(not_1_out));
  Multiplexer #(.width(32), .enable("false")) multiplexer_3 (
    .in0({32{1'b0}}), .in1(register_3_q), .out(Bout), .sel(not_1_out));
  Multiplexer #(.width(32), .enable("false")) multiplexer_4 (
    .in0({32{1'b0}}), .in1(register_4_q), .out(SEXout), .sel(not_1_out));
  Multiplexer #(.width(4), .enable("false")) multiplexer_5 (
    .in0(4'b0000), .in1(register_5_q), .out(OPout), .sel(not_1_out));
  Multiplexer #(.width(4), .enable("false")) multiplexer_6 (
    .in0(4'b0000), .in1(register_6_q), .out(RXout), .sel(not_1_out));
endmodule

module EX_MEM_Buffer (
  input  [23:0] ADDin,
  input  [31:0] ALUin,
  input  [31:0] DATAin,
  input  [3:0] OPin,
  input  [3:0] RXin,
  input  CLK,
  output [23:0] ADDout,
  output [31:0] ALUout,
  output [31:0] DATAin_2,
  output [3:0] OPout,
  output [3:0] RXout
);

  Register #(.width(24)) register_1 (.D(ADDin), .Q(ADDout), .clk(CLK));  // open: en, clr
  Register #(.width(32)) register_2 (.D(ALUin), .Q(ALUout), .clk(CLK));  // open: en, clr
  Register #(.width(32)) register_3 (.D(DATAin), .Q(DATAin_2), .clk(CLK));  // open: en, clr
  Register #(.width(4)) register_4 (.D(OPin), .Q(OPout), .clk(CLK));  // open: en, clr
  Register #(.width(4)) register_5 (.D(RXin), .Q(RXout), .clk(CLK));  // open: en, clr
endmodule

module MEM_WB_Buffer (
  input  [31:0] DATAin,
  input  [31:0] ADDRin,
  input  [3:0] OPin,
  input  [3:0] RXin,
  input  CLK,
  output [31:0] DATAin_2,
  output [31:0] ADDRout,
  output [3:0] OPout,
  output [3:0] RXout
);

  Register #(.width(32)) register_1 (.D(DATAin), .Q(DATAin_2), .clk(CLK));  // open: en, clr
  Register #(.width(32)) register_2 (.D(ADDRin), .Q(ADDRout), .clk(CLK));  // open: en, clr
  Register #(.width(4)) register_3 (.D(OPin), .Q(OPout), .clk(CLK));  // open: en, clr
  Register #(.width(4)) register_4 (.D(RXin), .Q(RXout), .clk(CLK));  // open: en, clr
endmodule

module ALU (
  input  [1:0] FUNC,
  input  [31:0] A,
  input  [31:0] B,
  output [31:0] OUT
);

  wire [31:0] adder_1_out, adder_2_out, nand_1_out, subtractor_1_out;

  Adder #(.width(32)) adder_1 (.a(A), .b(B), .out(adder_1_out), .cin(1'b0));  // open: cout
  assign nand_1_out = ~(A & B);  // NAND_Gate nand_1, 32 bits wide
  Subtractor #(.width(32)) subtractor_1 (.a(A), .b(B), .out(subtractor_1_out), .bin(1'b0));  // open: bout
  Adder #(.width(32)) adder_2 (.a(A), .b(B), .out(adder_2_out), .cin(1'b1));  // open: cout
  Multiplexer #(.select(2), .width(32), .disabled(0), .enable("false")) multiplexer_1 (
    .in0(adder_1_out), .in1(nand_1_out), .in2(subtractor_1_out), .in3(adder_2_out), .out(OUT), .sel(FUNC));

  // Notes on the sheet:
  //   DO NOT MODIFY THIS
endmodule

module SEXT (
  input  [31:0] Din,
  output [31:0] Dout
);


  assign Dout = {{13{Din[19]}}, Din[18:0]};
endmodule

module SRED (
  input  [31:0] Din,
  output [23:0] Dout
);


  assign Dout = Din[23:0];
endmodule

module IDRRControl (
  input  [3:0] RX,
  input  [3:0] RZ,
  input  [3:0] OPCode,
  output [3:0] RX_RZ
);

  Multiplexer #(.select(4), .width(4)) multiplexer_1 (
    .in0(RZ), .in1(RZ), .in2(RZ), .in3(RZ), .in4(RX), .in5(RX), .in6(RX), .out(RX_RZ), .sel(OPCode));  // open: in7, in8, in9, in10, in11, in12, in13, in14, in15, en
endmodule

module EXControl (
  input  [3:0] OPCode,
  output MUX,
  output [1:0] func
);

  Multiplexer #(.select(4)) multiplexer_1 (
    .in0(1'b0), .in1(1'b0), .in2(1'b1), .in3(1'b1), .in4(1'b1), .in5(1'b0), .in6(1'b0), .out(MUX),
    .sel(OPCode));  // open: in7, in8, in9, in10, in11, in12, in13, in14, in15, en
  Multiplexer #(.select(4), .width(2)) multiplexer_2 (
    .in0(2'b00), .in1(2'b01), .in2(2'b00), .in3(2'b00), .in4(2'b00), .in5(2'b10), .in6(2'b00), .out(func),
    .sel(OPCode));  // open: in7, in8, in9, in10, in11, in12, in13, in14, in15, en
endmodule

module MEMControl (
  input  [3:0] OPCode,
  output STR,
  output LD
);

  Multiplexer #(.select(4)) multiplexer_1 (
    .in0(1'b0), .in1(1'b0), .in2(1'b0), .in3(1'b0), .in4(1'b1), .in5(1'b0), .in6(1'b0), .in7(1'b0),
    .out(STR), .sel(OPCode));  // open: in8, in9, in10, in11, in12, in13, in14, in15, en
  Multiplexer #(.select(4)) multiplexer_2 (
    .in0(1'b0), .in1(1'b0), .in2(1'b0), .in3(1'b1), .in4(1'b0), .in5(1'b0), .in6(1'b0), .in7(1'b0), .out(LD),
    .sel(OPCode));  // open: in8, in9, in10, in11, in12, in13, in14, in15, en
endmodule

module WBControl (
  input  [3:0] OPCode,
  output WrEN,
  output MUX
);

  Multiplexer #(.select(4)) multiplexer_1 (
    .in0(1'b1), .in1(1'b1), .in2(1'b1), .in3(1'b1), .in4(1'b0), .in5(1'b0), .in6(1'b0), .out(WrEN),
    .sel(OPCode));  // open: in7, in8, in9, in10, in11, in12, in13, in14, in15, en
  Multiplexer #(.select(4)) multiplexer_2 (
    .in0(1'b1), .in1(1'b1), .in2(1'b1), .in3(1'b0), .in4(1'b0), .in5(1'b0), .in6(1'b0), .in7(1'b0),
    .in8(1'b0), .in9(1'b0), .out(MUX), .sel(OPCode));  // open: in10, in11, in12, in13, in14, in15, en

  // Notes on the sheet:
  //   Or do we do that in ID/RR Stage
  //   JALR store PC+1 into RY
endmodule

module MUXBox (
  input  EQ,
  input  [3:0] OPCode,
  output [1:0] Sel,
  output FLUSH
);

  wire comparator_1_eq;

  or or_1 (FLUSH, Sel[0], Sel[1]);
  and and_1 (Sel[0], EQ, comparator_1_eq);
  Comparator #(.width(4)) comparator_1 (.a(4'b0101), .b(OPCode), .eq(comparator_1_eq));  // open: gt, lt
  Comparator #(.width(4)) comparator_2 (.a(OPCode), .b(4'b0110), .eq(Sel[1]));  // open: gt, lt
endmodule

module StallCheck (
  input  [3:0] OPCode,
  input  [3:0] RX,
  input  [3:0] RY,
  input  [3:0] RZ,
  input  [3:0] ID_RROP,
  input  [1:0] PCMux,
  output [1:0] PCMuxout,
  output Stall1,
  output Stall2
);

  wire and_1_out, and_2_out, and_3_out, comparator_1_gt, comparator_2_lt, comparator_3_eq, comparator_4_eq,
       comparator_5_eq;

  Multiplexer #(.width(2), .enable("false")) multiplexer_1 (.in0(PCMux), .in1(2'b11), .out(PCMuxout), .sel(Stall1));
  or or_1 (Stall1, and_1_out, and_2_out);
  and and_1 (and_1_out, comparator_3_eq, comparator_4_eq);
  and and_2 (and_2_out, comparator_3_eq, comparator_5_eq);
  and and_3 (and_3_out, comparator_1_gt, comparator_2_lt);
  Comparator #(.width(4)) comparator_1 (.a(4'b0110), .b(ID_RROP), .gt(comparator_1_gt));  // open: eq, lt
  Comparator #(.width(4)) comparator_2 (.a(4'b0001), .b(ID_RROP), .lt(comparator_2_lt));  // open: gt, eq
  Comparator #(.width(4)) comparator_3 (.a(4'b0011), .b(OPCode), .eq(comparator_3_eq));  // open: gt, lt
  Comparator #(.width(4)) comparator_4 (.a(RX), .b(RY), .eq(comparator_4_eq));  // open: gt, lt
  Comparator #(.width(4)) comparator_5 (.a(RX), .b(RZ), .eq(comparator_5_eq));  // open: gt, lt

  assign Stall2 = Stall1;

  // Notes on the sheet:
  //   EXE Stage
  //   ID/RR Stage
endmodule

module Forward_Circ (
  input  [3:0] RY,
  input  [3:0] RZorRX,
  input  [3:0] EXERx,
  input  [3:0] MEMRx,
  input  [31:0] ExeOut,
  input  [31:0] MemOut,
  input  [3:0] WBRx,
  input  [31:0] WBOut,
  output FERY,
  output FERZ,
  output FMRY,
  output [31:0] ExeOutOut,
  output FMRZ,
  output FWRY,
  output [31:0] MEMOutOut,
  output FWRZ,
  output [31:0] WBOutOut
);

  wire comparator_3_eq, comparator_4_eq, comparator_5_eq, comparator_6_eq, or_1_out, or_2_out;

  Comparator #(.width(4)) comparator_1 (.a(RY), .b(EXERx), .eq(FERY));  // open: gt, lt
  Comparator #(.width(4)) comparator_2 (.a(RZorRX), .b(EXERx), .eq(FERZ));  // open: gt, lt
  Comparator #(.width(4)) comparator_3 (.a(RY), .b(MEMRx), .eq(comparator_3_eq));  // open: gt, lt
  Comparator #(.width(4)) comparator_4 (.a(MEMRx), .b(RZorRX), .eq(comparator_4_eq));  // open: gt, lt
  Comparator #(.width(4)) comparator_5 (.a(RY), .b(WBRx), .eq(comparator_5_eq));  // open: gt, lt
  Comparator #(.width(4)) comparator_6 (.a(WBRx), .b(RZorRX), .eq(comparator_6_eq));  // open: gt, lt
  and and_1 (FMRY, comparator_3_eq, ~FERY);  // AND_Gate
  and and_2 (FMRZ, comparator_4_eq, ~FERZ);  // AND_Gate
  or or_1 (or_1_out, FMRY, FERY);
  or or_2 (or_2_out, FMRZ, FERZ);
  and and_3 (FWRY, comparator_5_eq, ~or_1_out);  // AND_Gate
  and and_4 (FWRZ, comparator_6_eq, ~or_2_out);  // AND_Gate

  assign ExeOutOut = ExeOut;
  assign MEMOutOut = MemOut;
  assign WBOutOut = WBOut;

  // Notes on the sheet:
  //   It is RX when: JALR, BEQ, and SW
  //   ID/RR
  //   Priorities
endmodule
